# Fritzing sketch circuit (saved by Fritzing 0.9.9b)
breadboards: 1

parts:
  Part1 = Arduino Uno (Rev3)
  R1 = Resistor [tolerance=±5% resistance=220 package="0402 [SMD]"]
  R2 = Resistor [tolerance=±5% resistance=220 package="0402 [SMD]"]
  R3 = Resistor [tolerance=±5% resistance=220 package="0402 [SMD]"]
  R4 = Resistor [tolerance=±5% resistance=220 package="0402 [SMD]"]
  Q1 = NPN-Transistor [part_number=S8050 package="TO92 [THT]"]
  C1 = Electrolytic Capacitor [capacitance=10µF voltage=35V package="100 mil [THT, electrolytic]"]
  D1 = Rectifier Diode [part_number=1N4001 package="300 mil [THT]"]
  D2 = Rectifier Diode [part_number=1N4001 package="300 mil [THT]"]
  D3 = Rectifier Diode [part_number=1N4001 package="300 mil [THT]"]
  C2 = Electrolytic Capacitor [capacitance=1µF voltage=35V package="100 mil [THT, electrolytic]"]
  C3 = Electrolytic Capacitor [capacitance=1µF voltage=35V package="100 mil [THT, electrolytic]"]
  C4 = Electrolytic Capacitor [capacitance=1µF voltage=35V package="100 mil [THT, electrolytic]"]
  R6 = Resistor [tolerance=±5% resistance=220 power=0.25 package="0402 [SMD]"]
  R7 = Resistor [tolerance=±5% resistance=220 power=0.25 package="0402 [SMD]"]
  R9 = Resistor [tolerance=±5% resistance=1k power=0.25 package="0805 [SMD]"]
  U1 = attiny85 [package=dip]
  D4 = Rectifier Diode [part_number=1N4001 package="300 mil [THT]"]
  R8 = Resistor [tolerance=±5% resistance=220 power=0.25 package="0805 [SMD]"]

nets:
  N1: Part1.A0, R7.Pin_1, R8.Pin_0
  N2: Part1.D9_PWM, R4.Pin_1
  N3: Part1.D10_PWM/SS, U1.Pin_8
  N4: Part1.D11_PWM/MOSI, R3.Pin_1
  N5: Part1.D12/MISO, R2.Pin_1
  N6: Part1.D13/SCK, R1.Pin_1
  N7: Part1.GND, Q1.E, C1.-, U1.Pin_4, R8.Pin_1
  N8: Part1.D2, C2.-, C3.-
  N9: Part1.D3_PWM, C4.-
  N10: Part1.D4, D4.anode
  N11: Part1.D5_PWM, R6.Pin_1
  N12: R1.Pin_0, U1.Pin_7
  N13: R2.Pin_0, U1.Pin_6
  N14: R3.Pin_0, U1.Pin_5
  N15: R4.Pin_0, U1.Pin_2
  N16: Q1.B, R6.Pin_0
  N17: Q1.C, C1.+, D1.cathode, R7.Pin_0, R9.Pin_1
  N18: D1.anode, D2.cathode, C3.+
  N19: D2.anode, D3.cathode, C4.+
  N20: D3.anode, C2.+, D4.cathode
  N21: R9.Pin_0, U1.Pin_1
